// Logisim project Automatic light Detection (1).circ as structural Verilog: 1 circuit, main circuit main
module main (
  input  PWR,
  input  LDR,
  output LIGHT
);

  wire not_1_out;

  not not_1 (not_1_out, LDR);
  and and_1 (LIGHT, PWR, not_1_out);
endmodule
